# Fritzing sketch arduinoDUE_Wind (saved by Fritzing 0.9.3b)
stripboards: 1
breadboards: 1

parts:
  PUSHBUTTON = Pushbutton [package="[SMD]"]
  CL_SWITCH = SPST Switch [package=switch-spdt_kit]
  Power_Lever_POT_10K = POT [package=pot_mammoth]
  10K = 10K Ω Resistor [package="1206 [SMD]"]
  10K_2 = 10K Ω Resistor [package="1206 [SMD]"]
  Part1 = Arduino Due (Rev2b)
  100_ohm1 = 10K Ω Resistor [package="1206 [SMD]"]
  LM2908 = LM2907M [package=THT]
  10k_ohm1 = 10K Ω Resistor [package="1206 [SMD]"]
  100_ohm2 = 10K Ω Resistor [package="1206 [SMD]"]
  100k_ohm1 = 10K Ω Resistor [package="1206 [SMD]"]
  0_01_uF1 = Schottky Diode [part_number=1N5817 package="300 mil [THT]"]
  1_uF1 = Schottky Diode [part_number=1N5817 package="300 mil [THT]"]
  220_ohm1 = 1k Ω Resistor [package=THT]

nets (from the breadboard view):
  N1: PUSHBUTTON.Pin_1, PUSHBUTTON.Pin_2, 10K_2.Pin_0, Part1.D2_PWM
  N2: PUSHBUTTON.Pin_3, PUSHBUTTON.Pin_4, CL_SWITCH.S, Power_Lever_POT_10K.E, Part1.IOREF
  N3: CL_SWITCH.O, 10K.Pin_0
  N4: CL_SWITCH.P, Part1.D4_PWM/SS1
  N5: Power_Lever_POT_10K.S, 10K.Pin_1, 10K_2.Pin_1, Part1.GND
  N6: Power_Lever_POT_10K.A, Part1.A0
  N7: 100_ohm1.Pin_0, 100_ohm1.Pin_1, LM2908.+V, LM2908.Serial_In, LM2908.In_4_/_ADC_4, LM2908.In_3_/_Infrain, LM2908.In_2, LM2908.NC, LM2908.Out_5, LM2908.Out_4, LM2908.Out_3, LM2908.Out_2, LM2908.Out_1, 10k_ohm1.Pin_0, 10k_ohm1.Pin_1, 100_ohm2.Pin_0, 100_ohm2.Pin_1, 100k_ohm1.Pin_0, 100k_ohm1.Pin_1, 0_01_uF1.cathode, 0_01_uF1.anode, 1_uF1.cathode, 1_uF1.anode, 220_ohm1.Pin_0, 220_ohm1.Pin_1

notes:
  To ESC TTL Control
  to Fan Motor
  3.3V Rails
  Speed Sense F2V Circuit

custom parts:
  10K Ω Resistor: A generic resistor
  10K Ω Resistor: A generic resistor
  LM2907M: Texas Instruments Demodulator
  1k Ω Resistor: A generic resistor (0.25W)
