# Fritzing sketch mosfetter (saved by Fritzing 0.9.3b)
stripboards: 1

parts:
  U1 = IC, SIP package, 8 pins [chip_label=IC]
  Q2 = Basic FET N-Channel [package="TO220 [THT]"]
  Q3 = NPN-Transistor [package="TO92 [THT]"]

nets:
  N1: U1.pin1, U1.pin2, U1.pin3, U1.pin4, U1.pin5, U1.pin6, U1.pin7, Q2.gate, Q2.drain, Q2.source, Q3.E, Q3.B, Q3.C
