# Fritzing sketch speedSenseStripboard (saved by Fritzing 0.9.3b)
breadboards: 1
stripboards: 1

parts:
  LM2907 = LM2907M [package=THT]
  10k_ohm = 10K Ω Resistor [package="1206 [SMD]"]
  100_ohm = 10K Ω Resistor [package="1206 [SMD]"]
  100_ohm_2 = 10K Ω Resistor [package="1206 [SMD]"]
  100k_ohm = 10K Ω Resistor [package="1206 [SMD]"]
  0_01_uF = Schottky Diode [part_number=1N5817 package="300 mil [THT]"]
  1_uF = Schottky Diode [part_number=1N5817 package="300 mil [THT]"]
  220_ohm = 1k Ω Resistor [package=THT]

nets:
  N1: LM2907.+V, LM2907.NC#13, 100_ohm.Pin_0, 100_ohm_2.Pin_0, 100_ohm_2.Pin_1
  N2: LM2907.Serial_In, LM2907.NC#12, 0_01_uF.anode
  N3: LM2907.In_4_/_ADC_4, LM2907.In_3_/_Infrain, LM2907.Out_2, LM2907.Out_1, 10k_ohm.Pin_1, 100_ohm.Pin_1, 100k_ohm.Pin_0, 100k_ohm.Pin_1, 0_01_uF.cathode, 1_uF.cathode, 1_uF.anode, 220_ohm.Pin_1
  N4: LM2907.In_2, LM2907.Out_3, 10k_ohm.Pin_0
  N5: LM2907.NC#5, LM2907.NC#6, LM2907.Out_5, LM2907.Out_4

custom parts:
  LM2907M: Texas Instruments Demodulator
  10K Ω Resistor: A generic resistor
  1k Ω Resistor: A generic resistor (0.25W)
